# Fritzing sketch ds3231 i2c LCD (saved by Fritzing 0.9.3b)
breadboards: 1

parts:
  ZS-042_RTC1 = ZS-042 RTC Module
  Part1 = Arduino Uno (Rev3)
  LCD2004-I2C1 = LCD2004-I2C
  Mod1 = KY-004 Key Switch Module [package="Breakout board"]

nets:
  GND: ZS-042_RTC1.GND, Part1.GND, LCD2004-I2C1.GND, Mod1.-
  VCC: ZS-042_RTC1.VCC, Part1.5V, LCD2004-I2C1.VCC, Mod1.Vin
  N1: ZS-042_RTC1.SDA, Part1.A4/SDA, LCD2004-I2C1.SDA
  N2: ZS-042_RTC1.SCL, Part1.A5/SCL, LCD2004-I2C1.SCL
  N3: Part1.D2, Mod1.S

custom parts:
  LCD2004-I2C: A standard character display with 4x20 characters. Comes in many colors with LCM2004 IIC attached.
  KY-004 Key Switch Module: Arduino Key Switch Module Keyes KY-004 is a push button that will output a high signal when pressed.
