# Fritzing sketch ds3231 i2c LCD (saved by Fritzing 0.9.3b)
breadboards: 1

parts:
  ZS-042_RTC1 = ZS-042 RTC Module
  Part1 = Arduino Uno (Rev3)
  LCD2004-I2C1 = LCD2004-I2C

nets:
  GND: ZS-042_RTC1.GND, Part1.GND, LCD2004-I2C1.GND
  VCC: ZS-042_RTC1.VCC, Part1.5V, LCD2004-I2C1.VCC
  N1: ZS-042_RTC1.SDA, Part1.A4/SDA, LCD2004-I2C1.SDA
  N2: ZS-042_RTC1.SCL, Part1.A5/SCL, LCD2004-I2C1.SCL

custom parts:
  LCD2004-I2C: A standard character display with 4x20 characters. Comes in many colors with LCM2004 IIC attached.
