# Fritzing sketch mega_lcd_keypad_ds3231 (saved by Fritzing 0.9.3b)
breadboards: 1

parts:
  Part1 = Arduino Mega 2560 (Rev3)
  ZS-042_RTC1 = ZS-042 RTC Module
  Keypad4x1 = Keypad Membran 4x4
  LCD2004-I2C1 = LCD2004-I2C

nets:
  N1: Part1.D21/SCL, ZS-042_RTC1.SCL, LCD2004-I2C1.SCL
  N2: Part1.D20/SDA, ZS-042_RTC1.SDA, LCD2004-I2C1.SDA
  N3: Part1.D9_PWM, Keypad4x1.Pin1
  N4: Part1.D8_PWM, Keypad4x1.Pin2
  VCC: Part1.5V, ZS-042_RTC1.VCC, LCD2004-I2C1.VCC
  GND: Part1.GND, ZS-042_RTC1.GND, LCD2004-I2C1.GND
  N5: Part1.D2_PWM, Keypad4x1.Pin8
  N6: Part1.D3_PWM, Keypad4x1.Pin7
  N7: Part1.D4_PWM, Keypad4x1.Pin6
  N8: Part1.D5_PWM, Keypad4x1.Pin5
  N9: Part1.D6_PWM, Keypad4x1.Pin4
  N10: Part1.D7_PWM, Keypad4x1.Pin3

custom parts:
  Keypad Membran 4x4: Membrane Keypad 4x4 Matrix
  LCD2004-I2C: A standard character display with 4x20 characters. Comes in many colors with LCM2004 IIC attached.
