# Fritzing sketch sim900a_mega_lcd_keypad_ds3231_sdreader_reedwitch (saved by Fritzing 0.9.3b)
breadboards: 1

parts:
  Part1 = Arduino Mega 2560 (Rev3)
  ZS-042_RTC1 = ZS-042 RTC Module
  Keypad4x1 = Keypad Membran 4x4
  LCD2004-I2C1 = LCD2004-I2C
  Mod1 = Full Size SD Card Module
  Mod2 = KY-025 Reed Switch Module [package="Breakout board"]
  Part2 = Adafruit FONA - Mini Cellular GSM Breakout

nets:
  N1: Part1.D21/SCL, ZS-042_RTC1.SCL, LCD2004-I2C1.SCL
  N2: Part1.D20/SDA, ZS-042_RTC1.SDA, LCD2004-I2C1.SDA
  N3: Part1.D13_PWM, Part2.RXD_5V
  N4: Part1.D12_PWM, Part2.TXD_5V
  N5: Part1.D9_PWM, Keypad4x1.Pin1
  N6: Part1.D8_PWM, Keypad4x1.Pin2
  VCC: Part1.5V, ZS-042_RTC1.VCC, LCD2004-I2C1.VCC, Mod1.pin_6, Mod2.+
  GND: Part1.GND, ZS-042_RTC1.GND, LCD2004-I2C1.GND, Mod1.pin_1, Mod1.pin_16, Mod2.G, Part2.GND
  N7: Part1.D2_PWM, Keypad4x1.Pin8, Mod2.D0
  N8: Part1.D3_PWM, Keypad4x1.Pin7
  N9: Part1.D4_PWM, Keypad4x1.Pin6
  N10: Part1.D5_PWM, Keypad4x1.Pin5
  N11: Part1.D6_PWM, Keypad4x1.Pin4
  N12: Part1.D7_PWM, Keypad4x1.Pin3
  N13: Part1.D50, Mod1.pin_14
  N14: Part1.D51, Mod1.pin_10
  N15: Part1.D52, Mod1.pin_12
  N16: Part1.D53, Mod1.pin_8

custom parts:
  Keypad Membran 4x4: Membrane Keypad 4x4 Matrix
  LCD2004-I2C: A standard character display with 4x20 characters. Comes in many colors with LCM2004 IIC attached.
  Full Size SD Card Module: SD Card Module Slot Socket Reader For Arduino ARM MCU
  KY-025 Reed Switch Module: KY-025 Reed Switch Module, it reacts in the presence of a magnetic field.
  Adafruit FONA - Mini Cellular GSM Breakout: An all-in-one cellular phone module that lets you add voice, text, SMS and GPRS data to your project. Quad-band 850/900/1800/1900MHz - connect onto any global GSM network with any 2G SIM. Includes an onboard LiPoly battery charging circuitry so you can take your project on the go. Also works as an FM radio receiver.
