# Fritzing sketch sd card (saved by Fritzing 0.9.3b)

parts:
  Part1 = Arduino Uno (Rev3)
  sdCard1 = my_sdCard

nets:
  N1: Part1.D10_PWM/SS, sdCard1.CS
  N2: Part1.D11_PWM/MOSI, sdCard1.MOSI
  N3: Part1.D12/MISO, sdCard1.MISO
  N4: Part1.D13/SCK, sdCard1.SCK
  GND: Part1.GND, sdCard1.GND
  5V: Part1.5V, sdCard1.VCC

custom parts:
  my_sdCard: micro sdCard Adapter with 90º pin header. Use a filtering Capacitor between CS and GND if needed. PCB View Pinouts are Reversed for laying parallel on PCB using a 90º pin header.
