# Fritzing sketch sim800l_mega_lcd_keypad_ds3231_sdreader_reedwitch (saved by Fritzing 0.9.3b)
breadboards: 1

parts:
  Part1 = Arduino Mega 2560 (Rev3)
  ZS-042_RTC1 = ZS-042 RTC Module
  Keypad4x1 = Keypad Membran 4x4
  LCD2004-I2C1 = LCD2004-I2C
  Mod1 = Full Size SD Card Module
  Mod2 = KY-025 Reed Switch Module [package="Breakout board"]
  Part3 = Arduino Mega 2560 (Rev3)
  Reg2 = DC-DC CONVERTER [part_number=80633 package=dc-dc_converter]
  SIM800L2 = SIM800L
  R3 = Resistor [tolerance=±5% resistance=220 package=THT]
  R4 = Resistor [tolerance=±5% resistance=220 package=THT]

nets:
  N1: Part1.D9_PWM, Keypad4x1.Pin1
  N2: Part1.D8_PWM, Keypad4x1.Pin2
  VCC: Part1.5V, ZS-042_RTC1.VCC, LCD2004-I2C1.VCC, Mod1.pin_6, Mod2.+
  GND: Part1.GND, ZS-042_RTC1.GND, LCD2004-I2C1.GND, Mod1.pin_16, Mod2.G
  N3: Part1.D2_PWM, Keypad4x1.Pin8, Mod2.D0
  N4: Part1.D3_PWM, Keypad4x1.Pin7
  N5: Part1.D4_PWM, Keypad4x1.Pin6
  N6: Part1.D5_PWM, Keypad4x1.Pin5
  N7: Part1.D6_PWM, Keypad4x1.Pin4
  N8: Part1.D7_PWM, Keypad4x1.Pin3
  N9: Part1.D50, Mod1.pin_14
  N10: Part1.D51, Mod1.pin_10
  N11: Part1.D52, Mod1.pin_12
  N12: Part1.D53, Mod1.pin_8
  N13: ZS-042_RTC1.SDA, LCD2004-I2C1.SDA, Part3.D20/SDA
  N14: ZS-042_RTC1.SCL, LCD2004-I2C1.SCL, Part3.D21/SCL
  N15: Part3.D11_PWM, R3.Pin_0
  N16: Part3.D10_PWM, SIM800L2.TXD
  N17: Part3.GND, R4.Pin_1
  N18: Part3.D6_PWM, SIM800L2.RST
  N19: Reg2.OUT-, SIM800L2.GND
  N20: Reg2.OUT+, SIM800L2.NET
  N21: SIM800L2.RXD, R3.Pin_1

custom parts:
  Keypad Membran 4x4: Membrane Keypad 4x4 Matrix
  LCD2004-I2C: A standard character display with 4x20 characters. Comes in many colors with LCM2004 IIC attached.
  Full Size SD Card Module: SD Card Module Slot Socket Reader For Arduino ARM MCU
  KY-025 Reed Switch Module: KY-025 Reed Switch Module, it reacts in the presence of a magnetic field.
  DC-DC CONVERTER: WYHP 5A constant current/voltage manufactured by Shenzhen Weiyapuhua Technology Co., Ltd
  SIM800L: SIM800L is a miniature cellular module which allows for GPRS transmission, sending and receiving SMS and making and receiving voice calls. Low cost and small footprint and quad band frequency support make this module perfect solution for any project that require long range connectivity. After connecting power module boots up, searches for cellular network and login automatically. On board LED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
