# Fritzing sketch sim900 and reed (saved by Fritzing 0.9.3b)

parts:
  Part1 = Arduino Uno (Rev3)
  Mod1 = KY-025 Reed Switch Module [package="Breakout board"]
  Part2 = Adafruit FONA - Mini Cellular GSM Breakout

nets:
  N1: Part1.D8, Part2.RXD_5V
  GND: Part1.GND, Mod1.G, Part2.GND
  N2: Part1.D2, Mod1.D0
  N3: Part1.D7, Part2.TXD_5V
  N4: Part1.5V, Mod1.+

custom parts:
  KY-025 Reed Switch Module: KY-025 Reed Switch Module, it reacts in the presence of a magnetic field.
  Adafruit FONA - Mini Cellular GSM Breakout: An all-in-one cellular phone module that lets you add voice, text, SMS and GPRS data to your project. Quad-band 850/900/1800/1900MHz - connect onto any global GSM network with any 2G SIM. Includes an onboard LiPoly battery charging circuitry so you can take your project on the go. Also works as an FM radio receiver.
