# Fritzing sketch sim800l connection (saved by Fritzing 0.9.3b)

parts:
  Part1 = Arduino Mega 2560 (Rev3)
  Reg1 = DC-DC CONVERTER [part_number=80633 package=dc-dc_converter]
  SIM800L1 = SIM800L
  R1 = Resistor [tolerance=±5% resistance=220 package=THT]
  R2 = Resistor [tolerance=±5% resistance=220 package=THT]

nets:
  N1: Part1.D11_PWM, R1.Pin_0
  N2: Part1.D10_PWM, SIM800L1.TXD
  N3: Part1.GND, R2.Pin_1
  N4: Part1.D6_PWM, SIM800L1.RST
  N5: Reg1.OUT-, SIM800L1.GND
  N6: Reg1.OUT+, SIM800L1.NET
  N7: SIM800L1.RXD, R1.Pin_1

custom parts:
  DC-DC CONVERTER: WYHP 5A constant current/voltage manufactured by Shenzhen Weiyapuhua Technology Co., Ltd
  SIM800L: SIM800L is a miniature cellular module which allows for GPRS transmission, sending and receiving SMS and making and receiving voice calls. Low cost and small footprint and quad band frequency support make this module perfect solution for any project that require long range connectivity. After connecting power module boots up, searches for cellular network and login automatically. On board LED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
